// Logisim project DE0-CV_ITA.circ as structural Verilog: 6 circuits, main circuit main
module main (
);

  wire digital_oscilloscope_1_p10, K0, K1, K2, K3, L0, L1, L2, L3, L4, L5, L6, L7, L8, L9, S0, S1, S2, S3,
       S4, S5, S6, S7, S8, S9;
  wire [3:0] HEX0, HEX1, HEX2, HEX3, HEX4, HEX5;

  Hex_Digit_Display hex_digit_display_1 (.value(HEX5));  // open: dp
  LED u_L9 (.in(L9));
  LED u_L8 (.in(L8));
  // DipSwitch #(.NSwitches(1)) S9: pin names not known; wires that end beside it: S9, S9
  // DipSwitch #(.NSwitches(1)) S8: pin names not known; wires that end beside it: S8
  Hex_Digit_Display hex_digit_display_2 (.value(HEX3));  // open: dp
  Hex_Digit_Display hex_digit_display_3 (.value(HEX4));  // open: dp
  LED u_L6 (.in(L6));
  LED u_L7 (.in(L7));
  // DipSwitch #(.NSwitches(1)) S5: pin names not known; wires that end beside it: S5
  // DipSwitch #(.NSwitches(1)) S7: pin names not known; wires that end beside it: S7
  // DipSwitch #(.NSwitches(1)) S6: pin names not known; wires that end beside it: S6
  Hex_Digit_Display hex_digit_display_4 (.value(HEX2));  // open: dp
  LED u_L5 (.in(L5));
  LED u_L3 (.in(L3));
  LED u_L4 (.in(L4));
  // DipSwitch #(.NSwitches(1)) S4: pin names not known; wires that end beside it: S4
  // DipSwitch #(.NSwitches(1)) S3: pin names not known; wires that end beside it: S3
  counter_sync8 counter_sync8_1 (.CLK(S9), .CLR(S0), .C({L7, L6, L5, L4, L3, L2, L1, L0}));
  Hex_Digit_Display hex_digit_display_5 (.value(HEX0));  // open: dp
  Hex_Digit_Display hex_digit_display_6 (.value(HEX1));  // open: dp
  LED u_L0 (.in(L0));
  LED u_L2 (.in(L2));
  LED u_L1 (.in(L1));
  // DipSwitch #(.NSwitches(1)) S2: pin names not known; wires that end beside it: S2
  // DipSwitch #(.NSwitches(1)) S1: pin names not known; wires that end beside it: S1
  // DipSwitch #(.NSwitches(1)) S0: pin names not known; wires that end beside it: S0
  Button u_K2 (.out(K2));
  Button u_K3 (.out(K3));
  Button u_K0 (.out(K0));
  Button u_K1 (.out(K1));
  ROM #(.dataWidth(16), .Select("low")) rom_1 (
    .addr({L7, L6, L5, L4, L3, L2, L1, L0}), .data({HEX5, HEX4, HEX3, HEX2}));
  // Digital_Oscilloscope #(.nState(19)) digital_oscilloscope_1: pin names not known; wires that end beside it: S9, L0, L1, L2, L3, L4, L5, L6, L7, digital_oscilloscope_1_p10
  not not_1 (digital_oscilloscope_1_p10, S0);

  // Notes on the sheet:
  //   contents of rom_1 (hex, n*v repeats v):
  //   a3ad 4123 235 5 afdf ee 3523 fadf 4523 dfaf 5315 fadf 1235 fd34 dfad 351d 12df a1 43df 34ad
endmodule

module counter_async (
  input  CLK,
  input  [3:0] in_2,
  input  CLR,
  output C0,
  output C1,
  output C2,
  output C3
);

  wire and_1_out, or_1_out;
  wire [3:0] xor_1_out;

  T_Flip_Flop #(.trigger("falling"), .NegatePresetClear("true")) t_ff_1 (
    .clk(CLK), .T(1'b1), .Q(C0), .reset(and_1_out));  // open: Qn, preset
  buf and_1 (and_1_out, CLR);  // AND_Gate
  T_Flip_Flop #(.trigger("falling"), .NegatePresetClear("true")) t_ff_2 (
    .clk(C0), .T(1'b1), .Q(C1), .reset(and_1_out));  // open: Qn, preset
  or or_1 (or_1_out, xor_1_out[0], xor_1_out[1], xor_1_out[2], xor_1_out[3]);
  T_Flip_Flop #(.trigger("falling"), .NegatePresetClear("true")) t_ff_3 (
    .clk(C1), .T(1'b1), .Q(C2), .reset(and_1_out));  // open: Qn, preset
  assign xor_1_out = {C3, C2, C1, C0} ^ in_2;  // XOR_Gate xor_1, 4 bits wide
  T_Flip_Flop #(.trigger("falling"), .NegatePresetClear("true")) t_ff_4 (
    .clk(C2), .T(1'b1), .Q(C3), .reset(and_1_out));  // open: Qn, preset
endmodule

module counter_sync8 (
  input  CLK,
  input  CLR,
  output [7:0] C
);

  wire and_1_out, and_2_out, and_3_out, and_4_out, and_5_out, and_6_out;

  T_Flip_Flop #(.trigger("falling"), .NegatePresetClear("true")) t_ff_1 (
    .clk(CLK), .T(1'b1), .Q(C[0]), .reset(CLR));  // open: Qn, preset
  T_Flip_Flop #(.trigger("falling"), .NegatePresetClear("true")) t_ff_2 (
    .clk(CLK), .T(C[0]), .Q(C[1]), .reset(CLR));  // open: Qn, preset
  and and_1 (and_1_out, C[1], C[0]);
  T_Flip_Flop #(.trigger("falling"), .NegatePresetClear("true")) t_ff_3 (
    .clk(CLK), .T(and_1_out), .Q(C[2]), .reset(CLR));  // open: Qn, preset
  and and_2 (and_2_out, C[2], and_1_out);
  T_Flip_Flop #(.trigger("falling"), .NegatePresetClear("true")) t_ff_4 (
    .clk(CLK), .T(and_2_out), .Q(C[3]), .reset(CLR));  // open: Qn, preset
  and and_3 (and_3_out, C[3], and_2_out);
  T_Flip_Flop #(.trigger("falling"), .NegatePresetClear("true")) t_ff_5 (
    .clk(CLK), .T(and_3_out), .Q(C[4]), .reset(CLR));  // open: Qn, preset
  and and_4 (and_4_out, C[4], and_3_out);
  T_Flip_Flop #(.trigger("falling"), .NegatePresetClear("true")) t_ff_6 (
    .clk(CLK), .T(and_4_out), .Q(C[5]), .reset(CLR));  // open: Qn, preset
  and and_5 (and_5_out, C[5], and_4_out);
  T_Flip_Flop #(.trigger("falling"), .NegatePresetClear("true")) t_ff_7 (
    .clk(CLK), .T(and_5_out), .Q(C[6]), .reset(CLR));  // open: Qn, preset
  and and_6 (and_6_out, C[6], and_5_out);
  T_Flip_Flop #(.trigger("falling"), .NegatePresetClear("true")) t_ff_8 (
    .clk(CLK), .T(and_6_out), .Q(C[7]), .reset(CLR));  // open: Qn, preset
endmodule

module reg_parallel (
  input  [3:0] D,
  input  CLK,
  input  LOAD,
  input  CLR,
  output [3:0] out_5
);

  wire multiplexer_1_out, multiplexer_2_out, multiplexer_3_out, multiplexer_4_out;

  D_Flip_Flop #(.trigger("falling"), .NegatePresetClear("true")) d_ff_1 (
    .clk(CLK), .D(multiplexer_1_out), .Q(out_5[0]), .reset(CLR));  // open: Qn, preset
  Multiplexer #(.enable("false")) multiplexer_1 (.in0(out_5[0]), .in1(D[0]), .out(multiplexer_1_out), .sel(LOAD));
  Multiplexer #(.enable("false")) multiplexer_2 (.in0(out_5[1]), .in1(D[1]), .out(multiplexer_2_out), .sel(LOAD));
  D_Flip_Flop #(.trigger("falling"), .NegatePresetClear("true")) d_ff_2 (
    .clk(CLK), .D(multiplexer_2_out), .Q(out_5[1]), .reset(CLR));  // open: Qn, preset
  Multiplexer #(.enable("false")) multiplexer_3 (.in0(out_5[2]), .in1(D[2]), .out(multiplexer_3_out), .sel(LOAD));
  D_Flip_Flop #(.trigger("falling"), .NegatePresetClear("true")) d_ff_3 (
    .clk(CLK), .D(multiplexer_3_out), .Q(out_5[2]), .reset(CLR));  // open: Qn, preset
  Multiplexer #(.enable("false")) multiplexer_4 (.in0(out_5[3]), .in1(D[3]), .out(multiplexer_4_out), .sel(LOAD));
  D_Flip_Flop #(.trigger("falling"), .NegatePresetClear("true")) d_ff_4 (
    .clk(CLK), .D(multiplexer_4_out), .Q(out_5[3]), .reset(CLR));  // open: Qn, preset
endmodule

// parallel_serial
module parellel_to_serial (
  input  [3:0] P,
  input  ENABLE,
  input  CLK,
  input  CLR,
  output S
);

  wire d_ff_1_q, d_ff_2_q, d_ff_3_q, nand_1_out, nand_2_out, nand_3_out, nand_4_out;

  nand nand_1 (nand_1_out, ENABLE, P[1]);
  nand nand_2 (nand_2_out, ENABLE, P[0]);
  D_Flip_Flop #(.trigger("falling"), .NegatePresetClear("true")) d_ff_1 (
    .clk(CLK), .D(1'b0), .Q(d_ff_1_q), .preset(nand_2_out), .reset(CLR));  // open: Qn
  nand nand_3 (nand_3_out, ENABLE, P[2]);
  D_Flip_Flop #(.trigger("falling"), .NegatePresetClear("true")) d_ff_2 (
    .clk(CLK), .D(d_ff_1_q), .Q(d_ff_2_q), .preset(nand_1_out), .reset(CLR));  // open: Qn
  nand nand_4 (nand_4_out, ENABLE, P[3]);
  D_Flip_Flop #(.trigger("falling"), .NegatePresetClear("true")) d_ff_3 (
    .clk(CLK), .D(d_ff_2_q), .Q(d_ff_3_q), .preset(nand_3_out), .reset(CLR));  // open: Qn
  D_Flip_Flop #(.trigger("falling"), .NegatePresetClear("true")) d_ff_4 (
    .clk(CLK), .D(d_ff_3_q), .Q(S), .preset(nand_4_out), .reset(CLR));  // open: Qn
endmodule

module counter_sync4 (
  input  CLK,
  input  CLR,
  output [3:0] out_3
);

  wire and_1_out, and_2_out;

  T_Flip_Flop #(.NegatePresetClear("true")) t_ff_1 (
    .clk(CLK), .T(1'b1), .Q(out_3[0]), .reset(CLR));  // open: Qn, preset
  T_Flip_Flop #(.NegatePresetClear("true")) t_ff_2 (
    .clk(CLK), .T(out_3[0]), .Q(out_3[1]), .reset(CLR));  // open: Qn, preset
  T_Flip_Flop #(.NegatePresetClear("true")) t_ff_3 (
    .clk(CLK), .T(and_1_out), .Q(out_3[2]), .reset(CLR));  // open: Qn, preset
  and and_1 (and_1_out, out_3[1], out_3[0]);
  and and_2 (and_2_out, out_3[2], and_1_out);
  T_Flip_Flop #(.NegatePresetClear("true")) t_ff_4 (
    .clk(CLK), .T(and_2_out), .Q(out_3[3]), .reset(CLR));  // open: Qn, preset
endmodule
